# Fritzing sketch fstoptimer_uno (saved by Fritzing 0.9.2b)
breadboards: 1

parts:
  Part2 = Arduino Uno (Rev3)
  U5 = POT [package=pot_alpha_rv16af-20]
  S8 = Momentary Switch [package=ksa_sealed_tac_switch]
  S9 = Momentary Switch [package=ksa_sealed_tac_switch]
  S10 = Momentary Switch [package=ksa_sealed_tac_switch]
  S11 = Momentary Switch [package=ksa_sealed_tac_switch]
  S12 = Momentary Switch [package=ksa_sealed_tac_switch]
  S13 = Momentary Switch [package=ksa_sealed_tac_switch]
  U6 = RELAY-SOLIDSTATE [package=relay-s108t02]
  R2 = Resistor [tolerance=±5% resistance=220 package="2010 [SMD]"]
  U7 = LCD-16X2 [package=lcd-16x2]

nets:
  N1: Part2.A0, S13.3
  N2: Part2.A1, S11.3
  N3: Part2.A2, S10.3
  N4: Part2.A3, S12.3
  N5: Part2.A4/SDA, S8.3
  N6: Part2.A5/SCL, S9.3
  N7: Part2.D10_PWM/SS, U6.+
  N8: Part2.D11_PWM/MOSI, U7.E
  N9: Part2.D12/MISO, U7.RS
  N10: Part2.GND, U6.-
  N11: Part2.D2, U7.DB7
  N12: Part2.D3_PWM, U7.DB6
  N13: Part2.D4, U7.DB5
  N14: Part2.D5_PWM, U7.DB4
  N15: Part2.D6_PWM, R2.Pin_0
  5V: Part2.5V, U5.E, U7.VDD
  N16: U5.A, S8.1, S9.1, S10.1, S11.1, S12.1, S13.1, U7.VSS, U7.R_W, U7.K
  N17: U5.S, U7.VO
  N18: R2.Pin_1, U7.A
